// Logisim project BancDeRegistres.circ as structural Verilog: 1 circuit, main circuit BancRegistre
module BancRegistre (
  input  Clk,
  input  Reset,
  input  [2:0] RegDest,
  input  [31:0] DataIn,
  input  [2:0] RegA,
  input  [2:0] RegB,
  output [31:0] R0,
  output [31:0] R1,
  output [31:0] R2,
  output [31:0] R3,
  output [31:0] R4,
  output [31:0] R5,
  output [31:0] R6,
  output [31:0] R7,
  output [31:0] AOut,
  output [31:0] BOut
);

  wire [31:0] demultiplexer_1_out0, demultiplexer_1_out1, demultiplexer_1_out2, demultiplexer_1_out3,
       demultiplexer_1_out4, demultiplexer_1_out5, demultiplexer_1_out6, demultiplexer_1_out7,
       demultiplexer_2_out0, demultiplexer_3_out0;

  Register #(.width(32)) register_1 (.D(demultiplexer_1_out0), .clk(Clk), .Q(R0), .clr(Reset));  // open: en
  Demultiplexer #(.select(3), .width(32), .enable("false")) demultiplexer_1 (
    .out0(demultiplexer_1_out0), .out1(demultiplexer_1_out1), .out2(demultiplexer_1_out2),
    .out3(demultiplexer_1_out3), .out4(demultiplexer_1_out4), .out5(demultiplexer_1_out5),
    .out6(demultiplexer_1_out6), .out7(demultiplexer_1_out7), .in(DataIn), .sel(RegDest));
  Register #(.width(32)) register_2 (.D(demultiplexer_1_out1), .clk(Clk), .Q(R1), .clr(Reset));  // open: en
  Demultiplexer #(.select(3), .width(32), .enable("false")) demultiplexer_2 (
    .out0(demultiplexer_2_out0), .in(DataIn), .sel(RegA));  // open: out1, out2, out3, out4, out5, out6, out7
  Demultiplexer #(.select(3), .width(32), .enable("false")) demultiplexer_3 (
    .out0(demultiplexer_3_out0), .in(DataIn), .sel(RegB));  // open: out1, out2, out3, out4, out5, out6, out7
  Register #(.width(32)) register_3 (.D(demultiplexer_1_out2), .clk(Clk), .Q(R2), .clr(Reset));  // open: en
  Register #(.width(32)) register_4 (.D(demultiplexer_3_out0), .Q(BOut));  // open: en, clk, clr
  Register #(.width(32)) register_5 (.D(demultiplexer_1_out3), .clk(Clk), .Q(R3), .clr(Reset));  // open: en
  Register #(.width(32)) register_6 (.D(demultiplexer_2_out0), .Q(AOut));  // open: en, clk, clr
  Register #(.width(32)) register_7 (.D(demultiplexer_1_out4), .clk(Clk), .Q(R4), .clr(Reset));  // open: en
  Register #(.width(32)) register_8 (.D(demultiplexer_1_out5), .clk(Clk), .Q(R5), .clr(Reset));  // open: en
  Register #(.width(32)) register_9 (.D(demultiplexer_1_out6), .clk(Clk), .Q(R6), .clr(Reset));  // open: en
  Register #(.width(32)) register_10 (.D(demultiplexer_1_out7), .clk(Clk), .Q(R7), .clr(Reset));  // open: en
endmodule
