// Logisim project ALU.circ as structural Verilog: 3 circuits, main circuit ALU
module ALU (
  input  CarryIn,
  input  [31:0] A,
  input  [31:0] B,
  input  [3:0] Codop,
  input  [4:0] Shift,
  output [31:0] S,
  output [3:0] Flags
);

  wire adder_1_cout, adder_2_cout, bitselector_1_out, bitselector_2_out, bitselector_3_out,
       subtractor_1_bout, subtractor_2_bout, subtractor_3_bout;
  wire [31:0] A_and_B_out, A_and_NotB_out, a_fois_b_1_result, A_or_B_out, A_xor_B_out, adder_1_out,
       adder_2_out, and_1_out, not_B, shifter_1_out, shifter_2_out, shifter_3_out, shifter_4_out,
       subtractor_1_out, subtractor_2_out, subtractor_3_out;

  assign A_and_B_out = A & B;  // AND_Gate A_and_B, 32 bits wide
  assign A_xor_B_out = A ^ B;  // XOR_Gate A_xor_B, 32 bits wide
  Shifter #(.width(32)) shifter_1 (.in(B), .\dist (Shift), .out(shifter_1_out));
  Shifter #(.width(32), .shift("lr")) shifter_2 (.in(B), .\dist (Shift), .out(shifter_2_out));
  Shifter #(.width(32), .shift("ar")) shifter_3 (.in(B), .\dist (Shift), .out(shifter_3_out));
  Adder #(.width(32)) adder_1 (.a(A), .b(B), .out(adder_1_out), .cin(CarryIn), .cout(adder_1_cout));
  Subtractor #(.width(32)) subtractor_1 (.a(A), .b(B), .out(subtractor_1_out), .bin(CarryIn), .bout(subtractor_1_bout));
  Shifter #(.width(32), .shift("rr")) shifter_4 (.in(B), .\dist (Shift), .out(shifter_4_out));
  assign and_1_out = A & B;  // AND_Gate and_1, 32 bits wide
  Subtractor #(.width(32)) subtractor_2 (
    .a({32{1'b0}}), .b(A), .out(subtractor_2_out), .bout(subtractor_2_bout));  // open: bin
  Subtractor #(.width(32)) subtractor_3 (.a(A), .b(B), .out(subtractor_3_out), .bout(subtractor_3_bout));  // open: bin
  Adder #(.width(32)) adder_2 (.a(A), .b(B), .out(adder_2_out), .cout(adder_2_cout));  // open: cin
  assign A_or_B_out = A | B;  // OR_Gate A_or_B, 32 bits wide
  assign A_and_NotB_out = A & not_B;  // AND_Gate A_and_NotB, 32 bits wide
  assign not_B = ~B;  // NOT_Gate Not_B, 32 bits wide
  A_Fois_B a_fois_b_1 (.A(A), .B(B), .Result(a_fois_b_1_result));
  Multiplexer #(.select(4), .width(32), .enable("false")) multiplexer_1 (
    .in0(A_and_B_out), .in1(A_xor_B_out), .in2(shifter_1_out), .in3(shifter_2_out), .in4(shifter_3_out),
    .in5(adder_1_out), .in6(subtractor_1_out), .in7(shifter_4_out), .in8(and_1_out), .in9(subtractor_2_out),
    .in10(subtractor_3_out), .in11(adder_2_out), .in12(A_or_B_out), .in13(a_fois_b_1_result),
    .in14(A_and_NotB_out), .in15(not_B), .out(S), .sel(Codop));
  Multiplexer #(.select(4), .enable("false")) multiplexer_2 (
    .in0(1'b0), .in1(1'b0), .in2(1'b0), .in3(1'b0), .in4(1'b0), .in5(adder_1_cout), .in6(subtractor_1_bout),
    .in7(1'b0), .in8(1'b0), .in9(subtractor_2_bout), .in10(subtractor_3_bout), .in11(adder_2_cout),
    .in12(1'b0), .in13(1'b0), .in14(1'b0), .in15(1'b0), .out(Flags[2]), .sel(Codop));
  BitSelector #(.width(32)) bitselector_1 (.in(A), .out(bitselector_1_out), .sel({5{1'b1}}));
  BitSelector #(.width(32)) bitselector_2 (.in(B), .out(bitselector_2_out), .sel({5{1'b1}}));
  BitSelector #(.width(32)) bitselector_3 (.in(S), .out(bitselector_3_out), .sel({5{1'b1}}));
  Comparator #(.width(32)) comparator_1 (.a(S), .b({32{1'b0}}), .eq(Flags[1]), .lt(Flags[0]));  // open: gt
  OverFlow overflow_1 (
    .CodOp(Codop), .A(bitselector_1_out), .B(bitselector_2_out), .Res(bitselector_3_out), .OverFlow(Flags[3]));

  // Other names for the same wires on the sheet: Cod[3:0] = Codop; N = Flags[0]; Z = Flags[1]; C = Flags[2];
  //   V = Flags[3]

  // Notes on the sheet:
  //   Note: for ROR, C = N
  //   Note 2: assume that shift > 0 for LSL and LSR
endmodule

module OverFlow (
  input  [3:0] CodOp,
  input  A,
  input  B,
  input  Res,
  output OverFlow
);

  wire Add, and_1_out, and_2_out, and_3_out, and_4_out, and_5_out, and_6_out, and_7_out, and_8_out,
       comparator_1_eq, comparator_2_eq, comparator_4_eq, comparator_5_eq, not_1_out, not_2_out, not_3_out,
       not_4_out, not_5_out, not_6_out, or_3_out, or_4_out, Re, Sub;

  not not_1 (not_1_out, Res);
  not not_2 (not_2_out, A);
  not not_3 (not_3_out, B);
  not not_4 (not_4_out, B);
  not not_5 (not_5_out, A);
  not not_6 (not_6_out, Res);
  Comparator #(.width(4)) comparator_1 (.a(CodOp), .b(4'b1011), .eq(comparator_1_eq));  // open: gt, lt
  Comparator #(.width(4)) comparator_2 (.a(CodOp), .b(4'b0101), .eq(comparator_2_eq));  // open: gt, lt
  Comparator #(.width(4)) comparator_3 (.a(CodOp), .b(4'b1001), .eq(Re));  // open: gt, lt
  Comparator #(.width(4)) comparator_4 (.a(CodOp), .b(4'b0110), .eq(comparator_4_eq));  // open: gt, lt
  Comparator #(.width(4)) comparator_5 (.a(CodOp), .b(4'b1010), .eq(comparator_5_eq));  // open: gt, lt
  and and_1 (and_1_out, A, B, not_1_out);
  and and_2 (and_2_out, not_2_out, not_3_out, Res);
  and and_3 (and_3_out, A, not_4_out, Res);
  and and_4 (and_4_out, not_5_out, B, not_6_out);
  and and_5 (and_5_out, 1'b1, B, Res);
  or or_1 (Add, comparator_1_eq, comparator_2_eq);
  or or_2 (Sub, comparator_4_eq, comparator_5_eq);
  or or_3 (or_3_out, and_1_out, and_2_out);
  or or_4 (or_4_out, and_3_out, and_4_out);
  and and_6 (and_6_out, Re, and_5_out);
  and and_7 (and_7_out, Add, or_3_out);
  and and_8 (and_8_out, Sub, or_4_out);
  or or_5 (OverFlow, and_7_out, and_8_out, and_6_out);
endmodule

module A_Fois_B (
  input  [31:0] A,
  input  [31:0] B,
  output [31:0] Result
);

  wire [15:0] multiplier_1_out, multiplier_2_out, multiplier_3_out;
  wire [31:0] adder_1_out, bit_extender_1_out, bit_extender_2_out, bit_extender_3_out, shifter_1_out,
       shifter_2_out;

  // Probe on A
  // Probe on B
  Multiplier #(.width(16)) multiplier_1 (.a(A[15:0]), .b(B[31:16]), .out(multiplier_1_out));  // open: cin, cout
  Multiplier #(.width(16)) multiplier_2 (.a(A[15:0]), .b(B[15:0]), .out(multiplier_2_out));  // open: cin, cout
  Multiplier #(.width(16)) multiplier_3 (.a(A[31:16]), .b(B[15:0]), .out(multiplier_3_out));  // open: cin, cout
  assign bit_extender_1_out = {{16{multiplier_3_out[15]}}, multiplier_3_out};  // Bit_Extender bit_extender_1
  assign bit_extender_2_out = {{16{multiplier_1_out[15]}}, multiplier_1_out};  // Bit_Extender bit_extender_2
  assign bit_extender_3_out = {{16{multiplier_2_out[15]}}, multiplier_2_out};  // Bit_Extender bit_extender_3
  Shifter #(.width(32)) shifter_1 (.in(bit_extender_2_out), .\dist (5'b10000), .out(shifter_1_out));
  Shifter #(.width(32)) shifter_2 (.in(bit_extender_1_out), .\dist (5'b10000), .out(shifter_2_out));
  Adder #(.width(32)) adder_1 (.a(shifter_2_out), .b(bit_extender_3_out), .out(adder_1_out));  // open: cin, cout
  Adder #(.width(32)) adder_2 (.a(shifter_1_out), .b(adder_1_out), .out(Result));  // open: cin, cout
  // Probe on Result
endmodule
