// Logisim project Controller.circ as structural Verilog: 8 circuits, main circuit Controller
module Controller (
  input  [15:0] Inst,
  input  [3:0] Flags,
  input  Clk,
  input  Reset,
  output Carry,
  output DP_Shift,
  output Imm32_Enable,
  output [4:0] Imm5,
  output [31:0] Imm32,
  output [3:0] ALU_Opcode,
  output [2:0] Rm,
  output [2:0] Rn,
  output [2:0] Rd,
  output [31:0] RAM_Addr,
  output Load,
  output Store,
  output [7:0] PC
);

  wire Conditional_1_verified, Load_Store_1_pc_hold, not_1_out, Opcode_Decoder_1_conditional,
       Opcode_Decoder_1_data_processing, Opcode_Decoder_1_load_store, Opcode_Decoder_1_shift,
       Opcode_Decoder_1_sp_address, Shift_Add_Sub_Mov_1_carry, SP_Address_1_write_enable;
  wire [2:0] Data_Processing_1_rd, Data_Processing_1_rm, Data_Processing_1_rn, Load_Store_1_rd,
       Load_Store_1_rm, Shift_Add_Sub_Mov_1_rd, Shift_Add_Sub_Mov_1_rm, Shift_Add_Sub_Mov_1_rn;
  wire [3:0] Data_Processing_1_alu_opcode, Data_Processing_1_flags_update_mask, flags_apsr_1_flags_out,
       or_1_out, Shift_Add_Sub_Mov_1_alu_opcode, Shift_Add_Sub_Mov_1_flags_update_mask;
  wire [7:0] adder_1_out, adder_2_out, Conditional_1_offset;
  wire [31:0] SP_Address_1_new_stack_pointer, Stack_Pointer_q;

  Register #(.width(32)) Stack_Pointer (
    .D(SP_Address_1_new_stack_pointer), .en(SP_Address_1_write_enable), .clk(Clk), .Q(Stack_Pointer_q),
    .clr(Reset));
  Opcode_Decoder Opcode_Decoder_1 (
    .Opcode(Inst[15:10]), .Shift(Opcode_Decoder_1_shift), .Load_Store(Opcode_Decoder_1_load_store),
    .Conditional(Opcode_Decoder_1_conditional), .Data_Processing(Opcode_Decoder_1_data_processing),
    .SP_Address(Opcode_Decoder_1_sp_address));
  assign or_1_out = Data_Processing_1_flags_update_mask | Shift_Add_Sub_Mov_1_flags_update_mask;  // OR_Gate or_1, 4 bits wide
  Shift_Add_Sub_Mov Shift_Add_Sub_Mov_1 (
    .Carry(Shift_Add_Sub_Mov_1_carry), .Imm32_Enable(Imm32_Enable),
    .ALU_Opcode(Shift_Add_Sub_Mov_1_alu_opcode), .Rm(Shift_Add_Sub_Mov_1_rm), .Rn(Shift_Add_Sub_Mov_1_rn),
    .Rd(Shift_Add_Sub_Mov_1_rd), .Flags_Update_Mask(Shift_Add_Sub_Mov_1_flags_update_mask), .Imm5(Imm5),
    .Imm32(Imm32), .Instruction(Inst), .Enable(Opcode_Decoder_1_shift));
  Flags_APSR flags_apsr_1 (
    .Flags_In(or_1_out), .Update_Mask(Flags), .Clk(Clk), .Rst(Reset), .Flags_Out(flags_apsr_1_flags_out));
  Load_Store Load_Store_1 (
    .Rm(Load_Store_1_rm), .Instruction(Inst), .Rd(Load_Store_1_rd), .Load(Load),
    .Enable(Opcode_Decoder_1_load_store), .RAM_Addr(RAM_Addr), .Stack_Pointer(Stack_Pointer_q),
    .Store(Store), .Clk(Clk), .Reset(Reset), .PC_Hold(Load_Store_1_pc_hold));
  Conditional Conditional_1 (
    .Offset(Conditional_1_offset), .Instruction(Inst), .Enable(Opcode_Decoder_1_conditional),
    .Verified(Conditional_1_verified), .Z(flags_apsr_1_flags_out[2]), .V(flags_apsr_1_flags_out[0]),
    .N(flags_apsr_1_flags_out[3]), .C(flags_apsr_1_flags_out[1]));
  Data_Processing Data_Processing_1 (
    .Rn(Data_Processing_1_rn), .Instruction(Inst), .Rd(Data_Processing_1_rd),
    .Enable(Opcode_Decoder_1_data_processing), .Rm(Data_Processing_1_rm),
    .ALU_Opcode(Data_Processing_1_alu_opcode), .Flags_Update_Mask(Data_Processing_1_flags_update_mask));
  SP_Address SP_Address_1 (
    .New_Stack_Pointer(SP_Address_1_new_stack_pointer), .Write_Enable(SP_Address_1_write_enable),
    .Stack_Pointer(Stack_Pointer_q), .Instruction(Inst), .Enable(Opcode_Decoder_1_sp_address));
  Adder adder_1 (.a(8'h3), .b(Conditional_1_offset), .out(adder_1_out), .cin(1'b0));  // open: cout
  Adder adder_2 (.a(adder_1_out), .b(PC), .out(adder_2_out), .cin(1'b0));  // open: cout
  and and_1 (DP_Shift, Opcode_Decoder_1_shift, ~Opcode_Decoder_1_data_processing);  // AND_Gate
  not not_1 (not_1_out, Load_Store_1_pc_hold);
  Counter counter_1 (
    .clr(Reset), .load(Conditional_1_verified), .up(1'b1), .count(not_1_out), .clk(Clk), .D(adder_2_out),
    .Q(PC));  // open: carry
  Multiplexer #(.enable("false")) multiplexer_1 (
    .in0(flags_apsr_1_flags_out[1]), .in1(Shift_Add_Sub_Mov_1_carry), .out(Carry), .sel(DP_Shift));
  assign ALU_Opcode = Shift_Add_Sub_Mov_1_alu_opcode | Data_Processing_1_alu_opcode;  // OR_Gate or_2, 4 bits wide
  assign Rm = Shift_Add_Sub_Mov_1_rm | Data_Processing_1_rm | Load_Store_1_rm;  // OR_Gate or_3, 3 bits wide
  assign Rn = Shift_Add_Sub_Mov_1_rn | Data_Processing_1_rn;  // OR_Gate or_4, 3 bits wide
  assign Rd = Shift_Add_Sub_Mov_1_rd | Data_Processing_1_rd | Load_Store_1_rd;  // OR_Gate or_5, 3 bits wide

  // Notes on the sheet:
  //   Extract carry
  //   Extract Opcode
  //   IF Reg_Imm=1 THEN use shift value from register ELSE use shift value from Imm5
  //   Buffer flags for next instruction
  //   Add 3 to offset because ARM pre-increments PC
  //   and does an additionnal prefect operation
endmodule

module Conditional (
  input  Enable,
  input  [15:0] Instruction,
  input  N,
  input  Z,
  input  C,
  input  V,
  output [7:0] Offset,
  output Verified
);

  wire and_1_out, and_2_out, and_3_out, and_4_out, and_5_out, and_6_out, and_7_out, and_8_out, and_9_out,
       and_10_out, and_11_out, and_12_out, and_13_out, and_14_out, and_15_out, and_16_out, and_17_out,
       and_18_out, and_19_out, and_20_out, and_21_out, and_22_out, demultiplexer_1_out0,
       demultiplexer_1_out1, demultiplexer_1_out2, demultiplexer_1_out3, demultiplexer_1_out4,
       demultiplexer_1_out5, demultiplexer_1_out6, demultiplexer_1_out7, demultiplexer_1_out8,
       demultiplexer_1_out9, demultiplexer_1_out10, demultiplexer_1_out11, demultiplexer_1_out12,
       demultiplexer_1_out14, demultiplexer_1_out15, not_1_out, not_2_out, not_3_out, not_4_out, not_5_out,
       not_6_out, not_7_out, not_8_out, not_9_out, not_10_out, not_11_out, not_12_out, not_13_out,
       not_14_out, not_15_out, not_16_out, not_17_out, or_1_out, or_2_out, or_3_out, or_4_out;

  Demultiplexer #(.select(4), .enable("false")) demultiplexer_1 (
    .out0(demultiplexer_1_out0), .out1(demultiplexer_1_out1), .out2(demultiplexer_1_out2),
    .out3(demultiplexer_1_out3), .out4(demultiplexer_1_out4), .out5(demultiplexer_1_out5),
    .out6(demultiplexer_1_out6), .out7(demultiplexer_1_out7), .out8(demultiplexer_1_out8),
    .out9(demultiplexer_1_out9), .out10(demultiplexer_1_out10), .out11(demultiplexer_1_out11),
    .out12(demultiplexer_1_out12), .out13(Z), .out14(demultiplexer_1_out14), .out15(demultiplexer_1_out15),
    .in(Enable), .sel(Instruction[12:9]));
  not not_1 (not_1_out, V);
  not not_2 (not_2_out, N);
  not not_3 (not_3_out, V);
  not not_4 (not_4_out, N);
  not not_5 (not_5_out, Z);
  not not_6 (not_6_out, C);
  not not_7 (not_7_out, N);
  not not_8 (not_8_out, V);
  not not_9 (not_9_out, Z);
  not not_10 (not_10_out, C);
  and and_1 (and_1_out, V, N);
  not not_11 (not_11_out, V);
  and and_2 (and_2_out, not_11_out, not_12_out);
  not not_12 (not_12_out, N);
  and and_3 (and_3_out, V, N);
  not not_13 (not_13_out, V);
  and and_4 (and_4_out, not_13_out, not_14_out);
  not not_14 (not_14_out, N);
  not not_15 (not_15_out, Z);
  and and_5 (and_5_out, V, N);
  and and_6 (and_6_out, not_1_out, not_2_out);
  and and_7 (and_7_out, V, N);
  and and_8 (and_8_out, not_3_out, not_4_out);
  and and_9 (and_9_out, demultiplexer_1_out0, Z);
  and and_10 (and_10_out, not_5_out, demultiplexer_1_out1);
  and and_11 (and_11_out, demultiplexer_1_out2, C);
  and and_12 (and_12_out, not_6_out, demultiplexer_1_out3);
  and and_13 (and_13_out, demultiplexer_1_out4, N);
  and and_14 (and_14_out, not_7_out, demultiplexer_1_out5);
  and and_15 (and_15_out, demultiplexer_1_out6, V);
  and and_16 (and_16_out, not_8_out, demultiplexer_1_out7);
  and and_17 (and_17_out, demultiplexer_1_out8, C, not_9_out);
  and and_18 (and_18_out, demultiplexer_1_out9, not_10_out, Z);
  or or_1 (or_1_out, and_1_out, and_2_out);
  or or_2 (or_2_out, and_3_out, and_4_out);
  and and_19 (and_19_out, demultiplexer_1_out12, not_15_out, or_3_out);
  or or_3 (or_3_out, and_5_out, and_6_out);
  not not_16 (not_16_out, or_4_out);
  or or_4 (or_4_out, and_7_out, and_8_out);
  and and_20 (and_20_out, demultiplexer_1_out10, or_1_out);
  and and_21 (and_21_out, demultiplexer_1_out11, not_17_out);
  not not_17 (not_17_out, or_2_out);
  and and_22 (and_22_out, Z, Z, not_16_out);
  or or_5 (Verified, and_9_out, and_10_out, and_11_out, and_12_out, and_13_out, and_14_out, and_15_out, and_16_out, and_17_out, and_18_out, and_20_out, and_21_out, and_19_out, and_22_out, demultiplexer_1_out14);

  assign Offset = Instruction[8:1];

  // Other names for the same wires on the sheet: C_intern = C; N_intern = N; V_intern = V; Z_intern = Z
endmodule

module Opcode_Decoder (
  input  [5:0] Opcode,
  output Shift,
  output Load_Store,
  output Conditional,
  output Data_Processing,
  output SP_Address
);

  wire and_1_out, and_2_out, and_3_out, and_5_out, and_7_out, and_8_out, and_10_out, and_12_out, and_13_out,
       and_14_out, not_1_out, not_2_out, not_3_out, not_4_out, not_5_out, not_6_out, not_7_out, not_8_out,
       not_9_out, not_10_out, not_11_out;

  not not_1 (not_1_out, Opcode[3]);
  not not_2 (not_2_out, Opcode[2]);
  not not_3 (not_3_out, Opcode[1]);
  not not_4 (not_4_out, Opcode[0]);
  and and_1 (and_1_out, not_1_out, not_2_out);
  and and_2 (and_2_out, not_3_out, not_4_out);
  not not_5 (not_5_out, Opcode[4]);
  not not_6 (not_6_out, Opcode[3]);
  not not_7 (not_7_out, Opcode[3]);
  and and_3 (and_3_out, and_1_out, and_2_out);
  not not_8 (not_8_out, Opcode[4]);
  not not_9 (not_9_out, Opcode[5]);
  and and_4 (Shift, not_9_out, not_10_out);
  not not_10 (not_10_out, Opcode[4]);
  and and_5 (and_5_out, Opcode[5], not_5_out);
  and and_6 (Load_Store, and_5_out, and_7_out);
  and and_7 (and_7_out, not_6_out, Opcode[2]);
  and and_8 (and_8_out, Opcode[5], Opcode[4]);
  and and_9 (Conditional, and_8_out, and_10_out);
  and and_10 (and_10_out, not_7_out, Opcode[2]);
  not not_11 (not_11_out, Opcode[5]);
  and and_11 (Data_Processing, not_11_out, and_12_out);
  and and_12 (and_12_out, Opcode[4], and_3_out);
  and and_13 (and_13_out, Opcode[3], Opcode[2]);
  and and_14 (and_14_out, Opcode[5], not_8_out);
  and and_15 (SP_Address, and_13_out, and_14_out);

  // Other names for the same wires on the sheet: F = Opcode[0]; E = Opcode[1]; D = Opcode[2]; C = Opcode[3];
  //   B = Opcode[4]; A = Opcode[5]

  // Notes on the sheet:
  //   Shift, add, sub, mov
  //   Load/Store
  //   Conditional branch
  //   Data Processing
  //   SP Address
endmodule

module Data_Processing (
  input  Enable,
  input  [15:0] Instruction,
  output [2:0] Rm,
  output [2:0] Rn,
  output [2:0] Rd,
  output [3:0] Flags_Update_Mask,
  output [3:0] ALU_Opcode
);

  wire C, V;
  wire [2:0] demultiplexer_1_out0, demultiplexer_1_out1, demultiplexer_1_out2, demultiplexer_1_out3,
       demultiplexer_1_out4, demultiplexer_1_out5, demultiplexer_1_out6, demultiplexer_1_out7,
       demultiplexer_1_out8, demultiplexer_1_out9, demultiplexer_1_out10, demultiplexer_1_out11,
       demultiplexer_1_out12, demultiplexer_1_out13, demultiplexer_1_out14, demultiplexer_1_out15, or_1_out,
       or_2_out, or_3_out;

  Multiplexer #(.select(4)) multiplexer_1 (
    .in0(1'b0), .in1(1'b0), .in2(1'b1), .in3(1'b1), .in4(1'b1), .in5(1'b1), .in6(1'b1), .in7(1'b1),
    .in8(1'b0), .in9(1'b0), .in10(1'b0), .in11(1'b0), .in12(1'b0), .in13(1'b0), .in14(1'b0), .in15(1'b0),
    .out(C), .sel(Instruction[9:6]), .en(Enable));
  Demultiplexer #(.select(4), .width(3)) demultiplexer_1 (
    .out0(demultiplexer_1_out0), .out1(demultiplexer_1_out1), .out2(demultiplexer_1_out2),
    .out3(demultiplexer_1_out3), .out4(demultiplexer_1_out4), .out5(demultiplexer_1_out5),
    .out6(demultiplexer_1_out6), .out7(demultiplexer_1_out7), .out8(demultiplexer_1_out8),
    .out9(demultiplexer_1_out9), .out10(demultiplexer_1_out10), .out11(demultiplexer_1_out11),
    .out12(demultiplexer_1_out12), .out13(demultiplexer_1_out13), .out14(demultiplexer_1_out14),
    .out15(demultiplexer_1_out15), .in(Instruction[2:0]), .sel(Instruction[9:6]), .en(Enable));
  Multiplexer #(.select(4)) multiplexer_2 (
    .in0(1'b0), .in1(1'b0), .in2(1'b0), .in3(1'b0), .in4(1'b0), .in5(1'b1), .in6(1'b1), .in7(1'b0),
    .in8(1'b0), .in9(1'b0), .in10(1'b1), .in11(1'b1), .in12(1'b0), .in13(1'b0), .in14(1'b0), .in15(1'b0),
    .out(V), .sel(Instruction[9:6]), .en(Enable));
  Demultiplexer #(.width(3), .enable("false")) demultiplexer_2 (
    .out1(Rm), .in(Instruction[5:3]), .sel(Enable));  // open: out0
  assign or_1_out = demultiplexer_1_out0 | demultiplexer_1_out1 | demultiplexer_1_out2 | demultiplexer_1_out3 | demultiplexer_1_out4 | demultiplexer_1_out13 | demultiplexer_1_out5 | demultiplexer_1_out6 | demultiplexer_1_out7 | demultiplexer_1_out12 | demultiplexer_1_out14;  // OR_Gate or_1, 3 bits wide
  assign or_2_out = demultiplexer_1_out9 | demultiplexer_1_out15;  // OR_Gate or_2, 3 bits wide
  assign or_3_out = demultiplexer_1_out8 | demultiplexer_1_out11 | demultiplexer_1_out10;  // OR_Gate or_3, 3 bits wide
  assign Rd = or_1_out | or_2_out;  // OR_Gate or_4, 3 bits wide
  assign Rn = or_1_out | or_3_out;  // OR_Gate or_5, 3 bits wide
  Demultiplexer #(.width(4), .enable("false")) demultiplexer_3 (
    .out1(Flags_Update_Mask), .in({V, C, 2'b11}), .sel(Enable));  // open: out0
  Demultiplexer #(.width(4), .enable("false")) demultiplexer_4 (
    .out1(ALU_Opcode), .in(Instruction[9:6]), .sel(Enable));  // open: out0

  // Other names for the same wires on the sheet: ALU_OP[3:0] = Instruction[9:6]; b6 = Instruction[6];
  //   b7 = Instruction[7]; b8 = Instruction[8]; b9 = Instruction[9]; b0 = Instruction[0];
  //   b012[2:0] = Instruction[2:0]; b1 = Instruction[1]; b2 = Instruction[2]; b3 = Instruction[3];
  //   b345[2:0] = Instruction[5:3]; b4 = Instruction[4]; b5 = Instruction[5]; b10 = Instruction[10];
  //   b11 = Instruction[11]; b12 = Instruction[12]; b13 = Instruction[13]; b14 = Instruction[14];
  //   b15 = Instruction[15]

  // Notes on the sheet:
  //   Pull output low on Enable = 0
  //   Note 2: RSB instruction has Rn as 1st operand.
  //   MUL instruction has Rn as 1st operand and Rdm as 2nd operand
  //   For simplification purposes, Rm is used for 1st operand both here and in the ALU.
  //   Note: instructions that does not save the result will still have the second operand as the destination register, the ALU will copy the second register to the destination register
  //   Extract bytes
  //   Set result uppon alu opcode and enable
endmodule

module Shift_Add_Sub_Mov (
  input  [15:0] Instruction,
  input  Enable,
  output [3:0] ALU_Opcode,
  output [2:0] Rm,
  output [2:0] Rn,
  output [2:0] Rd,
  output [3:0] Flags_Update_Mask,
  output Carry,
  output Imm32_Enable,
  output [4:0] Imm5,
  output [31:0] Imm32
);

  wire Carry_t, Imm32_Enable_t, multiplexer_2_out, multiplexer_5_out, One_Last_Bits;
  wire [1:0] Before_Two_Last_Bits, Two_Last_Bits;
  wire [2:0] bitselector_5_out, bitselector_10_out, bitselector_11_out, bitselector_14_out,
       bitselector_17_out, Rd_t, Rm_t, Rn_t;
  wire [3:0] ALU, Flags, multiplexer_4_out, multiplexer_6_out, multiplexer_19_out;
  wire [4:0] bitselector_16_out, Imm5_t;
  wire [5:0] bitselector_13_out;
  wire [7:0] bitselector_9_out, bitselector_15_out;
  wire [8:0] bitselector_3_out;
  wire [10:0] bitselector_2_out;
  wire [12:0] bitselector_1_out;
  wire [31:0] bitselector_4_out, bitselector_12_out, Imm32_t, multiplexer_1_out, multiplexer_3_out,
       negator_1_out;

  BitSelector #(.width(16), .group(13)) bitselector_1 (.in(Instruction), .out(bitselector_1_out), .sel(1'b1));
  BitSelector #(.width(16), .group(11)) bitselector_2 (.in(Instruction), .out(bitselector_2_out), .sel(1'b1));
  BitSelector #(.width(16), .group(9)) bitselector_3 (.in(Instruction), .out(bitselector_3_out), .sel(1'b1));
  BitSelector #(.width(3), .group(32)) bitselector_4 (.in(bitselector_5_out), .out(bitselector_4_out), .sel(1'b0));
  BitSelector #(.width(16), .group(3)) bitselector_5 (.in(Instruction), .out(bitselector_5_out), .sel(3'b010));
  BitSelector #(.width(13)) bitselector_6 (.in(bitselector_1_out), .out(One_Last_Bits), .sel(4'b0000));
  BitSelector #(.width(11), .group(2)) bitselector_7 (.in(bitselector_2_out), .out(Two_Last_Bits), .sel(3'b000));
  BitSelector #(.width(9), .group(2)) bitselector_8 (.in(bitselector_3_out), .out(Before_Two_Last_Bits), .sel(3'b000));
  Multiplexer #(.select(2), .width(32), .enable("false")) multiplexer_1 (
    .in0({32{1'b0}}), .in1({32{1'b0}}), .in2(bitselector_4_out), .in3(bitselector_4_out),
    .out(multiplexer_1_out), .sel(Before_Two_Last_Bits));
  Multiplexer #(.select(2), .enable("false")) multiplexer_2 (
    .in0(1'b0), .in1(1'b0), .in2(1'b1), .in3(1'b1), .out(multiplexer_2_out), .sel(Before_Two_Last_Bits));
  Multiplexer #(.select(2), .width(32), .enable("false")) multiplexer_3 (
    .in0({32{1'b0}}), .in1({32{1'b0}}), .in2({32{1'b0}}), .in3(multiplexer_1_out), .out(multiplexer_3_out),
    .sel(Two_Last_Bits));
  Multiplexer #(.select(2), .width(4), .enable("false")) multiplexer_4 (
    .in0(4'b0101), .in1(4'b0110), .in2(4'b0101), .in3(4'b0110), .out(multiplexer_4_out),
    .sel(Before_Two_Last_Bits));
  Multiplexer #(.select(2), .enable("false")) multiplexer_5 (
    .in0(1'b0), .in1(1'b0), .in2(1'b0), .in3(multiplexer_2_out), .out(multiplexer_5_out), .sel(Two_Last_Bits));
  BitSelector #(.width(16), .group(8)) bitselector_9 (.in(Instruction), .out(bitselector_9_out), .sel(1'b0));
  BitSelector #(.width(16), .group(3)) bitselector_10 (.in(Instruction), .out(bitselector_10_out), .sel(3'b001));
  BitSelector #(.width(16), .group(3)) bitselector_11 (.in(Instruction), .out(bitselector_11_out), .sel(3'b010));
  Multiplexer #(.select(2), .width(4), .enable("false")) multiplexer_6 (
    .in0(4'b1110), .in1(4'b1110), .in2(4'b1110), .in3(4'b1111), .out(multiplexer_6_out), .sel(Two_Last_Bits));
  BitSelector #(.group(32)) bitselector_12 (.in(bitselector_9_out), .out(bitselector_12_out), .sel(1'b0));
  Negator #(.width(32)) negator_1 (.in(bitselector_12_out), .out(negator_1_out));
  BitSelector #(.width(16), .group(6)) bitselector_13 (.in(Instruction), .out(bitselector_13_out), .sel(2'b01));
  BitSelector #(.width(16), .group(3)) bitselector_14 (.in(Instruction), .out(bitselector_14_out), .sel(3'b000));
  BitSelector #(.width(16), .group(8)) bitselector_15 (.in(Instruction), .out(bitselector_15_out), .sel(1'b1));
  Multiplexer #(.enable("false")) multiplexer_7 (
    .in0(multiplexer_5_out), .in1(1'b1), .out(Imm32_Enable_t), .sel(One_Last_Bits));
  Multiplexer #(.select(2), .enable("false")) multiplexer_8 (
    .in0(1'b0), .in1(1'b1), .in2(1'b0), .in3(1'b1), .out(Carry_t), .sel(Before_Two_Last_Bits));
  Multiplexer #(.width(32), .enable("false")) multiplexer_9 (
    .in0(multiplexer_3_out), .in1(negator_1_out), .out(Imm32_t), .sel(One_Last_Bits));
  Multiplexer #(.width(4), .enable("false")) multiplexer_10 (.in0(4'b0000), .in1(ALU), .out(ALU_Opcode), .sel(Enable));
  Multiplexer #(.width(3), .enable("false")) multiplexer_11 (.in0(3'b000), .in1(Rm_t), .out(Rm), .sel(Enable));
  Multiplexer #(.width(3), .enable("false")) multiplexer_12 (.in0(3'b000), .in1(Rn_t), .out(Rn), .sel(Enable));
  Multiplexer #(.width(3), .enable("false")) multiplexer_13 (.in0(3'b000), .in1(Rd_t), .out(Rd), .sel(Enable));
  Multiplexer #(.width(4), .enable("false")) multiplexer_14 (
    .in0(4'b0000), .in1(Flags), .out(Flags_Update_Mask), .sel(Enable));
  Multiplexer #(.enable("false")) multiplexer_15 (.in0(1'b0), .in1(Carry_t), .out(Carry), .sel(Enable));
  Multiplexer #(.enable("false")) multiplexer_16 (.in0(1'b0), .in1(Imm32_Enable_t), .out(Imm32_Enable), .sel(Enable));
  Multiplexer #(.width(5), .enable("false")) multiplexer_17 (.in0({5{1'b0}}), .in1(Imm5_t), .out(Imm5), .sel(Enable));
  Multiplexer #(.width(32), .enable("false")) multiplexer_18 (
    .in0({32{1'b0}}), .in1(Imm32_t), .out(Imm32), .sel(Enable));
  Multiplexer #(.select(2), .width(4), .enable("false")) multiplexer_19 (
    .in0(4'b0010), .in1(4'b0011), .in2(4'b0100), .in3(multiplexer_4_out), .out(multiplexer_19_out),
    .sel(Two_Last_Bits));
  BitSelector #(.width(6), .group(5)) bitselector_16 (.in(bitselector_13_out), .out(bitselector_16_out), .sel(1'b0));
  BitSelector #(.group(3)) bitselector_17 (.in(bitselector_15_out), .out(bitselector_17_out), .sel(2'b00));
  Multiplexer #(.width(4), .enable("false")) multiplexer_20 (
    .in0(multiplexer_6_out), .in1(4'b1100), .out(Flags), .sel(One_Last_Bits));
  Multiplexer #(.width(4), .enable("false")) multiplexer_21 (
    .in0(multiplexer_19_out), .in1(4'b1001), .out(ALU), .sel(One_Last_Bits));
  Multiplexer #(.select(2), .width(5), .enable("false")) multiplexer_22 (
    .in0(bitselector_16_out), .in1(bitselector_16_out), .in2(bitselector_16_out), .in3({5{1'b0}}),
    .out(Imm5_t), .sel(Two_Last_Bits));
  Multiplexer #(.select(2), .width(3), .enable("false")) multiplexer_23 (
    .in0(bitselector_10_out), .in1(bitselector_10_out), .in2(bitselector_10_out), .in3(bitselector_11_out),
    .out(Rm_t), .sel(Two_Last_Bits));
  BitSelector #(.width(16), .group(3)) bitselector_18 (.in(Instruction), .out(Rn_t), .sel(3'b001));
  Multiplexer #(.width(3), .enable("false")) multiplexer_24 (
    .in0(bitselector_14_out), .in1(bitselector_17_out), .out(Rd_t), .sel(One_Last_Bits));

  // Notes on the sheet:
  //   Note 3: Imm32_Enable forces the use of the immediate for Rm register
  //   Note: ALU uses Rn register for shifts. Use Rn instead of Rm for shifts (immediate) here too
  //   Note 2: MOV uses RSB ALU opcode with Imm8 reversed so that it is copied to output register
endmodule

module Load_Store (
  input  Enable,
  input  Clk,
  input  [15:0] Instruction,
  input  [31:0] Stack_Pointer,
  input  Reset,
  output [2:0] Rd,
  output [2:0] Rm,
  output Store,
  output Load,
  output PC_Hold,
  output [31:0] RAM_Addr
);

  wire and_3_out, not_1_out, not_2_out, or_1_out;
  wire [31:0] bit_extender_1_out;

  not not_1 (not_1_out, Instruction[11]);
  and and_1 (Store, Instruction[11], Clk, Enable);
  and and_2 (Load, Enable, Clk, not_1_out);
  assign bit_extender_1_out = {{24{1'b0}}, Instruction[7:0]};  // Bit_Extender bit_extender_1
  Adder #(.width(32)) adder_1 (.a(bit_extender_1_out), .b(Stack_Pointer), .out(RAM_Addr));  // open: cin, cout
  or or_1 (or_1_out, Load, Store);
  not not_2 (not_2_out, PC_Hold);
  Register #(.width(1)) register_1 (.D(and_3_out), .clk(Clk), .Q(PC_Hold), .clr(Reset));  // open: en
  and and_3 (and_3_out, or_1_out, not_2_out);

  assign Rd = Instruction[10:8];
  assign Rm = Instruction[10:8];

  // Other names for the same wires on the sheet: clock_ls = Clk; Enab_ls = Enable

  // Notes on the sheet:
  //   Delay load and hold PC for 1 cycle for the RAM to send out requested data 
endmodule

module SP_Address (
  input  Enable,
  input  [15:0] Instruction,
  input  [31:0] Stack_Pointer,
  output Write_Enable,
  output [31:0] New_Stack_Pointer
);

  wire [31:0] adder_1_out, bit_extender_1_out, demultiplexer_1_out0, demultiplexer_1_out1, subtractor_1_out;

  Demultiplexer #(.width(32), .enable("false")) demultiplexer_1 (
    .out0(demultiplexer_1_out0), .out1(demultiplexer_1_out1), .in(bit_extender_1_out), .sel(Instruction[7]));
  assign bit_extender_1_out = {{25{Instruction[6]}}, Instruction[6:0]};  // Bit_Extender bit_extender_1
  Adder #(.width(32)) adder_1 (.a(demultiplexer_1_out0), .b(Stack_Pointer), .out(adder_1_out));  // open: cin, cout
  Subtractor #(.width(32)) subtractor_1 (
    .a(Stack_Pointer), .b(demultiplexer_1_out1), .out(subtractor_1_out));  // open: bin, bout
  Multiplexer #(.width(32)) multiplexer_1 (
    .in0(adder_1_out), .in1(subtractor_1_out), .out(New_Stack_Pointer), .sel(Instruction[7]), .en(Enable));

  assign Write_Enable = Enable;

  // Other names for the same wires on the sheet: imm7[6:0] = Instruction[6:0]; Op_code = Instruction[7]

  // Notes on the sheet:
  //   Pull output low on Enable = 0
  //   Deux cas possibles pour l'Opcode:
  //   - 0 : Addition avec le Stack_Pointer
  //   - 1 : Soustraction avec le Stack_Pointer
endmodule

module Flags_APSR (
  input  [3:0] Flags_In,
  input  [3:0] Update_Mask,
  input  Clk,
  input  Rst,
  output [3:0] Flags_Out
);

  wire register_1_q, register_3_q, register_4_q, register_5_q, ResetSynchrone, undriven, undriven_2,
       undriven_3, undriven_4, undriven_5;

  and and_1 (ResetSynchrone, Clk, Rst);
  Register #(.width(1)) register_1 (
    .D(undriven), .en(undriven_2), .Q(register_1_q), .clk(undriven_3), .clr(undriven_4));
  Register #(.width(1)) register_2 (
    .D(undriven), .en(undriven_2), .Q(register_1_q), .clk(undriven_3), .clr(undriven_4));
  Register #(.width(1)) register_3 (.D(Flags_In[1]), .clk(Clk), .Q(register_3_q));  // open: en, clr
  Register #(.width(1)) register_4 (.D(Flags_In[2]), .clk(Clk), .Q(register_4_q));  // open: en, clr
  Register #(.width(1)) register_5 (.D(Flags_In[3]), .clk(Clk), .Q(register_5_q));  // open: en, clr
  Register #(.width(1)) register_6 (
    .D(undriven_5), .en(Update_Mask[0]), .clk(Clk), .Q(Flags_Out[0]), .clr(ResetSynchrone));
  Register #(.width(1)) register_7 (
    .D(register_3_q), .en(Update_Mask[1]), .clk(Clk), .Q(Flags_Out[1]), .clr(ResetSynchrone));
  Register #(.width(1)) register_8 (
    .D(register_4_q), .en(Update_Mask[2]), .Q(Flags_Out[2]), .clr(ResetSynchrone));  // open: clk
  Register #(.width(1)) register_9 (
    .D(register_5_q), .en(Update_Mask[3]), .clk(Clk), .Q(Flags_Out[3]), .clr(ResetSynchrone));

  // Other names for the same wires on the sheet: clocktest = Clk; Reset = Rst; V_update = Update_Mask[0];
  //   C_update = Update_Mask[1]; Z_update = Update_Mask[2]; N_update = Update_Mask[3]

  // Notes on the sheet:
  //   Negative
  //   Current V flag
  //   Current C flag
  //   Current Z flag
  //   Current N flag
endmodule
